# Fritzing sketch Digital Inputs Logger Pi (saved by Fritzing 0.9.3b)
circuit board: 6.5cm x 5.6cm
breadboards: 1

parts:
  Raspberry_Pi_1 = Raspberry Pi 3 [part_number=RPI-3-V1.2]
  J1 = screw terminal, 8 pins
  R1 = Resistor [tolerance=±5% resistance=1k package=THT]
  R2 = Resistor [tolerance=±5% resistance=1k package=THT]
  R3 = Resistor [tolerance=±5% resistance=1k package=THT]
  R4 = Resistor [tolerance=±5% resistance=1k package=THT]
  R5 = Resistor [tolerance=±5% resistance=1k package=THT]
  R6 = Resistor [tolerance=±5% resistance=1k package=THT]
  R7 = Resistor [tolerance=±5% resistance=1k package=THT]
  R8 = Resistor [tolerance=±5% resistance=1k package=THT]
  R9 = Resistor [tolerance=±5% resistance=1k package=THT]
  R10 = Resistor [tolerance=±5% resistance=1k package=THT]
  R11 = Resistor [tolerance=±5% resistance=1k package=THT]
  R12 = Resistor [tolerance=±5% resistance=1k package=THT]
  R13 = Resistor [tolerance=±5% resistance=1k package=THT]
  R14 = female pin header, 9 pins [form="♀ (female)" part_number="8 x 10K"]
  R15 = female pin header, 9 pins [form="♀ (female)" part_number="8 x 10K"]
  D1 = Rectifier Diode [part_number=1N4001 package="300 mil [THT]"]
  D2 = Rectifier Diode [part_number=1N4001 package="300 mil [THT]"]
  D3 = Rectifier Diode [part_number=1N4001 package="300 mil [THT]"]
  D4 = Rectifier Diode [part_number=1N4001 package="300 mil [THT]"]
  D5 = Rectifier Diode [part_number=1N4001 package="300 mil [THT]"]
  D6 = Rectifier Diode [part_number=1N4001 package="300 mil [THT]"]
  D7 = Rectifier Diode [part_number=1N4001 package="300 mil [THT]"]
  D8 = Rectifier Diode [part_number=1N4001 package="300 mil [THT]"]
  D9 = Rectifier Diode [part_number=1N4001 package="300 mil [THT]"]
  D10 = Rectifier Diode [part_number=1N4001 package="300 mil [THT]"]
  D11 = Rectifier Diode [part_number=1N4001 package="300 mil [THT]"]
  D12 = Rectifier Diode [part_number=1N4001 package="300 mil [THT]"]
  D13 = Rectifier Diode [part_number=1N4001 package="300 mil [THT]"]
  J2 = screw terminal, 8 pins

nets:
  3V3: Raspberry_Pi_1.3v3, Raspberry_Pi_1.3V3, R14.pin1, R15.pin1
  N1: Raspberry_Pi_1.GPIO4, R1.Pin_1
  N2: Raspberry_Pi_1.GND, J1.pin1, J2.pin1
  N3: Raspberry_Pi_1.GPIO17, R2.Pin_1
  N4: Raspberry_Pi_1.GPIO27, R3.Pin_1
  N5: Raspberry_Pi_1.GPIO22, R4.Pin_1
  N6: Raspberry_Pi_1.GPIO5, R8.Pin_1
  N7: Raspberry_Pi_1.GPIO6, R10.Pin_1
  N8: Raspberry_Pi_1.GPIO26, R12.Pin_1
  N9: Raspberry_Pi_1.GPIO21, R13.Pin_1
  N10: Raspberry_Pi_1.GPIO20, R11.Pin_1
  N11: Raspberry_Pi_1.GPIO12, R9.Pin_1
  N12: Raspberry_Pi_1.GPIO25, R7.Pin_1
  N13: Raspberry_Pi_1.GPIO24, R6.Pin_1
  N14: Raspberry_Pi_1.GPIO23, R5.Pin_1
  N15: Raspberry_Pi_1.5V, J2.pin2
  N16: J1.pin2, D7.cathode
  N17: J1.pin3, D8.cathode
  N18: J1.pin4, D9.cathode
  N19: J1.pin5, D10.cathode
  N20: J1.pin6, D11.cathode
  N21: J1.pin7, D12.cathode
  N22: J1.pin8, D13.cathode
  N23: R1.Pin_0, R14.pin2, D1.anode
  N24: R2.Pin_0, R14.pin3, D2.anode
  N25: R3.Pin_0, R14.pin4, D3.anode
  N26: R4.Pin_0, R14.pin5, D4.anode
  N27: R5.Pin_0, R14.pin6, D5.anode
  N28: R6.Pin_0, R14.pin7, D6.anode
  N29: R7.Pin_0, R14.pin8, D7.anode
  N30: R8.Pin_0, R15.pin2, D8.anode
  N31: R9.Pin_0, R15.pin3, D9.anode
  N32: R10.Pin_0, R15.pin4, D10.anode
  N33: R11.Pin_0, R15.pin5, D11.anode
  N34: R12.Pin_0, R15.pin6, D12.anode
  N35: R13.Pin_0, R15.pin7, D13.anode
  N36: D1.cathode, J2.pin3
  N37: D2.cathode, J2.pin4
  N38: D3.cathode, J2.pin5
  N39: D4.cathode, J2.pin6
  N40: D5.cathode, J2.pin7
  N41: D6.cathode, J2.pin8

notes:
  B1->|GND|5V| 1| 2| 3| 4| 5| 6|
  B2->|GND| 7| 8| 9|10|11|12|13|
  GND
  B2
  B1
  Digital Inputs Logger Pi
  By GJ
